# Fritzing sketch HUZZAH_IMU_RTC_Serial (saved by Fritzing 0.9.3b)
breadboards: 1

parts:
  Adafruit_HUZZAH_ESP8266_Breakout1 = Adafruit HUZZAH ESP8266 Breakout [part_number=2471]
  Part1 = Real Time Clock Module - DS1307 RTC Breakout Board
  S1 = Momentary Switch [package=ksa_sealed_tac_switch]
  S2 = Momentary Switch [package=ksa_sealed_tac_switch]
  R1 = Resistor [tolerance=±5% resistance=10k package="2512 [SMD]"]
  R1_2 = Resistor [tolerance=±5% resistance=10k package="2512 [SMD]"]
  R1_3 = Resistor [tolerance=±5% resistance=10k package="2010 [SMD]"]
  R1_4 = Resistor [tolerance=±5% resistance=10k package="1206 [SMD]"]
  R1_5 = Resistor [tolerance=±5% resistance=10k package="1206 [SMD]"]
  R2 = Resistor [tolerance=±5% resistance=10k package="1206 [SMD]"]
  MPU9250_MPU-1 = SparkFun IMU Breakout - MPU-9250 [part_number=" SEN-13762"]
  Part2 = JeePlug experimenter's board  # not connected

nets:
  GND: Adafruit_HUZZAH_ESP8266_Breakout1.GND, Part1.GND, R1.Pin_1, R1_2.Pin_1, R1_3.Pin_1, R1_4.Pin_1, R1_5.Pin_1, R2.Pin_1
  N1: Adafruit_HUZZAH_ESP8266_Breakout1.#12, S2.1
  N2: Adafruit_HUZZAH_ESP8266_Breakout1.#14, S1.1
  N3: Adafruit_HUZZAH_ESP8266_Breakout1.3V, Part1.5V, S1.4, S2.4
  N4: Part1.SDA, MPU9250_MPU-1.VDDIO, MPU9250_MPU-1.!CS, MPU9250_MPU-1.INT
  N5: S1.2, R1.Pin_0, R1_2.Pin_0, R1_3.Pin_0, R1_4.Pin_0, R1_5.Pin_0
  N6: S2.2, R2.Pin_0
